# Fritzing sketch bme280-wiring (saved by Fritzing 1.0.6)
breadboards: 1

parts:
  A1 = Esp32-c3 super mini
  A2 = GY-BMP280 Breakout

nets:
  N1: A1.Pin_4, A2.Pin_4
  N2: A1.Pin_5, A2.Pin_3
  N3: A1.Pin_14, A2.Pin_1, A2.Pin_5
  N4: A1.Pin_15, A2.Pin_2, A2.Pin_6

custom parts:
  Esp32-c3 super mini: ESP32-C3 Development Board ESP32 SuperMini Development Board ESP32 Development Board WiFi Bluetooth.
