# Fritzing sketch bme280-ads1115-wiring (saved by Fritzing 1.0.6)
breadboards: 1

parts:
  A1 = Esp32-c3 super mini
  A2 = GY-BMP280 Breakout
  GY-ADS1 = GY-ADS1115 16Bit I2C ADC [part_number="Adafruit #1085"]
  U1 = POT [knob_status=50% power=0.5W package=alps_pot]

nets:
  N1: A1.Pin_4, A2.Pin_4, GY-ADS1.SDA
  N2: A1.Pin_5, A2.Pin_3, GY-ADS1.SCL
  N3: A1.Pin_14, A2.Pin_1, A2.Pin_5, GY-ADS1.VDD, U1.A
  N4: A1.Pin_15, A2.Pin_2, A2.Pin_6, GY-ADS1.ADDR, GY-ADS1.GND, U1.E
  N5: GY-ADS1.AIN0, U1.S

custom parts:
  Esp32-c3 super mini: ESP32-C3 Development Board ESP32 SuperMini Development Board ESP32 Development Board WiFi Bluetooth.
  GY-ADS1115 16Bit I2C ADC: For microcontrollers without an analog-to-digital converter or when you want a higher-precision ADC, the ADS1115 provides 16-bit precision at 860 samples/second over I2C. The chip can be configured as 4 single-ended input channels, or two differential channels. As a nice bonus, it even includes a programmable gain amplifier, up to x16, to help boost up smaller single/differential signals to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
