# Fritzing sketch bme280-ads1115-ldr-humidity-wiring (saved by Fritzing 0.9.3b)
breadboards: 1

parts:
  A1 = Esp32-c3 super mini
  A2 = GY-BMP280 Breakout
  GY-ADS1 = GY-ADS1115 16Bit I2C ADC [part_number="Adafruit #1085"]
  R2 = Resistor [tolerance=±5% power=0.25W resistance=4.7k package=THT]
  Part1 = FC-28 Soil Hygrometer Module
  Part2 = FC-28 Soil Hygrometer Module - Probe
  R3 = Photocell (LDR) [package=THT]

nets:
  N1: A1.Pin_4, A2.Pin_4, GY-ADS1.SDA
  N2: A1.Pin_5, A2.Pin_3, GY-ADS1.SCL
  VDD: A1.Pin_14, A2.Pin_1, A2.Pin_5, GY-ADS1.VDD, Part1.VCC, R3.pin_1
  GND: A1.Pin_15, A2.Pin_2, A2.Pin_6, GY-ADS1.ADDR, GY-ADS1.GND, R2.Pin_1, Part1.GND
  N3: GY-ADS1.AIN1, Part1.AO
  N4: GY-ADS1.AIN0, R2.Pin_0, R3.pin_0
  N5: Part1.POS, Part2.POS
  N6: Part1.NEG, Part2.NEG

custom parts:
  Esp32-c3 super mini: ESP32-C3 Development Board ESP32 SuperMini Development Board ESP32 Development Board WiFi Bluetooth.
  GY-ADS1115 16Bit I2C ADC: For microcontrollers without an analog-to-digital converter or when you want a higher-precision ADC, the ADS1115 provides 16-bit precision at 860 samples/second over I2C. The chip can be configured as 4 single-ended input channels, or two differential channels. As a nice bonus, it even includes a programmable gain amplifier, up to x16, to help boost up smaller single/differential signals to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
  FC-28 Soil Hygrometer Module: The FC-28 is a soil hygrometer module that uses the Texas Instruments LM393 comparator chip to provide an analog measurement of soil humidity. The digital output is high when soil moisture is over a certain threshold, as determined by adjusting the potentiometer.
  FC-28 Soil Hygrometer Module - Probe: The FC-28 is a soil hygrometer module that uses the Texas Instruments LM393 comparator chip to provide an analog measurement of soil humidity.
