# Fritzing sketch bme280-ads1115-ldr-humidity-irlz44n-hx711-wiring (saved by Fritzing 1.0.6)
breadboards: 1

parts:
  A1 = Esp32-c3 super mini
  A2 = GY-BMP280 Breakout
  GY-ADS1 = GY-ADS1115 16Bit I2C ADC [part_number="Adafruit #1085"]
  R2 = Resistor [tolerance=±5% power=0.25W resistance=4.7k package=THT]
  Part1 = FC-28 Soil Hygrometer Module
  Part2 = FC-28 Soil Hygrometer Module - Probe
  Q1 = MOSFET-NCHANNEL [package=to220v]
  R4 = Resistor [tolerance=±5% resistance=47 package="2010 [SMD]"]
  M1 = DC Motor [voltage_(max)=6V voltage_(min)=3V]
  VCC1 = Battery block 9V [internal_resistance=0.1Ω]
  R3 = Photocell (LDR) [power=0.25W dark_resistance_@0.01lx=300kΩ light_resistance_@100lx=400Ω luminance=10lx package=THT]
  Part3 = HX711 Weighing Sensor Module

nets:
  N1: A1.Pin_1, R4.Pin_1
  N2: A1.Pin_4, A2.Pin_4, GY-ADS1.SDA
  N3: A1.Pin_5, A2.Pin_3, GY-ADS1.SCL
  N4: A1.Pin_7, Part3.DO/RX
  N5: A1.Pin_8, Part3.CK/TX
  VCC: A1.Pin_14, A2.Pin_1, A2.Pin_5, GY-ADS1.VDD, Part1.VCC, R3.pin_1, Part3.VCC
  GND: A1.Pin_15, A2.Pin_2, A2.Pin_6, GY-ADS1.ADDR, GY-ADS1.GND, R2.Pin_1, Part1.GND, Q1.S, VCC1.-, Part3.GND
  N6: GY-ADS1.AIN1, Part1.AO
  N7: GY-ADS1.AIN0, R2.Pin_0, R3.pin_0
  N8: Part1.POS, Part2.POS
  N9: Part1.NEG, Part2.NEG
  N10: Q1.G, R4.Pin_0
  N11: Q1.D, M1.pin_2
  N12: M1.pin_1, VCC1.+

custom parts:
  Esp32-c3 super mini: ESP32-C3 Development Board ESP32 SuperMini Development Board ESP32 Development Board WiFi Bluetooth.
  GY-ADS1115 16Bit I2C ADC: For microcontrollers without an analog-to-digital converter or when you want a higher-precision ADC, the ADS1115 provides 16-bit precision at 860 samples/second over I2C. The chip can be configured as 4 single-ended input channels, or two differential channels. As a nice bonus, it even includes a programmable gain amplifier, up to x16, to help boost up smaller single/differential signals to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
  FC-28 Soil Hygrometer Module: The FC-28 is a soil hygrometer module that uses the Texas Instruments LM393 comparator chip to provide an analog measurement of soil humidity. The digital output is high when soil moisture is over a certain threshold, as determined by adjusting the potentiometer.
  FC-28 Soil Hygrometer Module - Probe: The FC-28 is a soil hygrometer module that uses the Texas Instruments LM393 comparator chip to provide an analog measurement of soil humidity.
