# Fritzing sketch power supply (saved by Fritzing 1.0.3b)

parts:
  Part1 = MCP73871 [part_number=MCP package=VQFN]
  MOD1 = Multi booster
  U1 = LIPO-110mAh [package=lipo-110]
  A1 = Esp32-c3 super mini
  PV1 = Generic Small 6V Solar Panel

nets:
  N1: Part1.OUT, MOD1.BAT+
  N2: Part1.Vss#9, MOD1.BAT-, MOD1.GND, A1.Pin_15
  N3: Part1.Vss#10, U1.-, PV1.-
  N4: Part1.VBAT, U1.+
  N5: Part1.IN, PV1.+
  N6: MOD1.V+, A1.Pin_14

custom parts:
  MCP73871: The MCP73871 device is a fully integrated linear solution for system load sharing and Li-Ion/Li-Polymer battery charge management with AC-DC wall adapter and USB port power sources selection. It is also capable of autonomous power source selection between input and battery. Along with its small physical size, the low number of required external components makes the device ideally suited for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
  Multi booster: Input voltage range: 2.5V + Current: 1A Boost output voltage: 5V/ 8V/ 9V 12V ------------ A B VOUT ------------ 0 0 5V 0 1 8V 1 0 9V 1 1 12V ------------
  Esp32-c3 super mini: ESP32-C3 Development Board ESP32 SuperMini Development Board ESP32 Development Board WiFi Bluetooth.
